# Fritzing sketch wiring (saved by Fritzing 0.9.6b)
circuit board: 8.46667cm x 5.64444cm
breadboards: 1

parts:
  Mod1 = Raspberry Pi Pico
  DS3231_RTC = ZS-042 RTC Module
  use_analog_voltmeter_0-3V = 7-Segment Panel Voltmeter
  IC1 = IC, DIP package, 14 pins [chip_label=74AHCT125N]
  Part1 = Display LED de 8 dígitos basado en MAX7219

nets:
  N1: Mod1.pin_1, DS3231_RTC.SDA
  N2: Mod1.pin_2, DS3231_RTC.SCL
  GND: Mod1.pin_3, Mod1.pin_8, Mod1.pin_13, Mod1.pin_18, Mod1.pin_23, Mod1.pin_28, Mod1.pin_33, Mod1.pin_38, Mod1.pin_42, DS3231_RTC.GND, use_analog_voltmeter_0-3V.V-, IC1.pin1, IC1.pin4, IC1.pin7, IC1.pin13, Part1.GND
  N3: Mod1.pin_7, IC1.pin2
  N4: Mod1.pin_9, IC1.pin5
  N5: Mod1.pin_10, IC1.pin12
  N6: Mod1.pin_34, use_analog_voltmeter_0-3V.V+
  N7: Mod1.pin_36, DS3231_RTC.VCC
  N8: Mod1.pin_40, IC1.pin14, Part1.VCC
  N9: IC1.pin3, Part1.CS
  N10: IC1.pin6, Part1.CLK
  N11: IC1.pin11, Part1.DIN

notes:
  5V rail from VBUS (use a 5V supply)

custom parts:
  Raspberry Pi Pico: Raspberry Pi Pico. Based around the RP2040 microcontroller the Pico is a low cost microcontroller device bringing Raspberry Pi quality, cost, and easy of use to the microcontroller space. Jan 2021, Split part in to two versions: tht (this one) and SMD. This one will drill holes for a .1 in header in pcb to allow plugging in the module as well as providing pads to solder the module to the top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
  7-Segment Panel Voltmeter: 7-Segment Panel Voltmeter (4.5 - 30V)
